# Fritzing sketch arduino_mqtt (saved by Fritzing 0.8.3b)
breadboards: 1

parts:
  Composants1 = Arduino Board Ethernet
  LED1 = LED - 5mm [color="Red (633nm)" package="5 mm [THT]"]
  LED2 = LED - 5mm [color="Green (570nm)" package="5 mm [THT]"]
  R1 = Photocell (LDR) [package=THT]
  R2 = Resistor [tolerance=±5% resistance=220 package=THT]
  R3 = Resistor [tolerance=±5% resistance=220 package=THT]

nets:
  N1: Composants1.D9_PWM, LED1.anode
  N2: Composants1.GND, R1.pin_0, R3.Pin_0
  N3: Composants1.A4, R1.pin_1, R2.Pin_1
  N4: Composants1.D6_PWM, LED2.anode
  N5: Composants1.5V, R2.Pin_0
  N6: LED1.cathode, LED2.cathode, R3.Pin_1
